# Fritzing sketch Win10IoT Thermo Diagram Cobbler (saved by Fritzing 0.9.2b)
breadboards: 1

parts:
  LED1 = LED - 5mm [color="Red (633nm)" package="5 mm [THT]"]
  R1 = Resistor [tolerance=±5% resistance=220 package="0603 [SMD]"]
  R2 = Resistor [tolerance=±5% resistance=220 package="0603 [SMD]"]
  DHT1 = DHT11 Humitidy and Temperature Sensor
  Raspberry_Pi2 = Raspberry Pi B+
  J1 = T Cobbler Plus

nets:
  N1: LED1.cathode, J1.GND#5
  N2: LED1.anode, R1.Pin_0
  VDD: R2.Pin_0, DHT1.VDD, J1.3V3
  N3: R2.Pin_1, DHT1.DATA
  N4: DHT1.GND, J1.GND#8
  3V3: Raspberry_Pi2.3v3, Raspberry_Pi2.3V3, J1.3.3V
  N5: Raspberry_Pi2.GPIO2, J1.GPIO_2
  N6: Raspberry_Pi2.GPIO3, J1.GPIO_3
  N7: Raspberry_Pi2.GPIO4, J1.GPIO_4
  N8: Raspberry_Pi2.GND, J1.GND#46, J1.GND#49, J1.GND#54, J1.GND#60, J1.GND#65, J1.GND#70, J1.GND#74, J1.GND#79
  N9: Raspberry_Pi2.GPIO17, J1.GPIO_17
  N10: Raspberry_Pi2.GPIO27, J1.GPIO_27
  N11: Raspberry_Pi2.GPIO22, J1.GPIO_22
  N12: Raspberry_Pi2.GPIO10, J1.GPIO_10
  N13: Raspberry_Pi2.GPIO9, J1.GPIO_9
  N14: Raspberry_Pi2.GPIO11, J1.GPIO_11
  N15: Raspberry_Pi2.ID_SD, J1.ID_SD
  N16: Raspberry_Pi2.GPIO5, J1.GPIO_5
  N17: Raspberry_Pi2.GPIO6, J1.GPIO_6
  N18: Raspberry_Pi2.GPIO13, J1.GPIO_13
  N19: Raspberry_Pi2.GPIO19, J1.GPIO_19
  N20: Raspberry_Pi2.GPIO26, J1.GPIO_26
  N21: Raspberry_Pi2.GPIO21, J1.GPIO_21
  N22: Raspberry_Pi2.GPIO20, J1.GPIO_20
  N23: Raspberry_Pi2.GPIO16, J1.GPIO_16
  N24: Raspberry_Pi2.GPIO12, J1.GPIO_12
  N25: Raspberry_Pi2.ID_SC, J1.ID_SC
  N26: Raspberry_Pi2.GPIO7, J1.GPIO_7
  N27: Raspberry_Pi2.GPIO8, J1.GPIO_8
  N28: Raspberry_Pi2.GPIO25, J1.GPIO_25
  N29: Raspberry_Pi2.GPIO24, J1.GPIO_24
  N30: Raspberry_Pi2.GPIO23, J1.GPIO_23
  N31: Raspberry_Pi2.GPIO18, J1.GPIO_18
  N32: Raspberry_Pi2.GPIO15, J1.GPIO_15
  N33: Raspberry_Pi2.GPIO14, J1.GPIO_14
  5V: Raspberry_Pi2.5V, J1.5V

custom parts:
  DHT11 Humitidy and Temperature Sensor: DHT11 Humidity and Temperature Sensor
  T Cobbler Plus: The T-Cobbler Plus is an add on prototyping board from Adafruit specifically designed for the Raspberry Pi B+ that can break out all those tasty power, GPIO, I2C and SPI pins from the 40-pin header onto a solderless breadboard. This set will make "cobbling together" prototypes with the Pi super easy. The T-Cobbler Plus can plug into any solderless breadboard.
