# Fritzing sketch Win10IoT Thermo Diagram (saved by Fritzing 0.9.2b)
breadboards: 1

parts:
  Raspberry_Pi1 = Raspberry Pi B rev2
  LED1 = LED - 5mm [color="Red (633nm)" package="5 mm [THT]"]
  R1 = Resistor [tolerance=±5% resistance=220 package="0603 [SMD]"]
  R2 = Resistor [tolerance=±5% resistance=220 package="0603 [SMD]"]
  DHT1 = DHT11 Humitidy and Temperature Sensor

nets:
  3V3: Raspberry_Pi1.3V3, R2.Pin_0, DHT1.VDD
  GND: Raspberry_Pi1.GND, LED1.cathode, DHT1.GND
  N1: Raspberry_Pi1.GPIO_4, R2.Pin_1, DHT1.DATA
  N2: Raspberry_Pi1.GPIO_25, R1.Pin_1
  N3: LED1.anode, R1.Pin_0

custom parts:
  DHT11 Humitidy and Temperature Sensor: DHT11 Humidity and Temperature Sensor
